# Fritzing sketch DC_Motor (saved by Fritzing 0.9.3b)
circuit board: 8.46667cm x 5.64444cm
breadboards: 1

parts:
  U1 = lolin
  BATT1 = 4xAA Switchable Battery Pack w/JST connector
  IC1 = ULN2803A [package=THT]
  M1 = DC Motor

nets (from the schematic view):
  N1: U1.connector20, BATT1.NEG, IC1.0V
  N2: U1.connector33, IC1.In_1
  N3: BATT1.POS, IC1.COM_-_Common, M1.pin_2
  N4: IC1.Out_1, M1.pin_1

custom parts:
  4xAA Switchable Battery Pack w/JST connector: 4xAA Switchable Battery Pack with JST connector

// code stored in the sketch: DC_Motor.ino
// https://www.sparkfun.com/datasheets/IC/uln2803a.pdf
// https://techtutorialsx.com/2016/09/12/esp8266-controlling-a-motor-with-the-uln2803a/
