# Fritzing sketch Sweep_esp32 (saved by Fritzing 0.9.3b)
breadboards: 1

parts:
  U1 = lolin
  J1 = Basic Servo
  BATT1 = 4xAA Switchable Battery Pack w/JST connector

nets:
  N1: U1.connector20, J1.gnd, BATT1.NEG
  N2: U1.connector33, J1.pulse
  N3: J1.vcc, BATT1.POS

custom parts:
  4xAA Switchable Battery Pack w/JST connector: 4xAA Switchable Battery Pack with JST connector
